# Fritzing sketch BT-HC05 (saved by Fritzing 0.8.7b)

parts:
  Part1 = Arduino Uno (Rev3)
  Part2 = Bluetooth HC-05 Macho

nets:
  N1: Part1.D10_PWM/SS, Part2.TXD
  N2: Part1.D11_PWM/MOSI, Part2.RXD
  GND: Part1.GND, Part2.GND
  5V: Part1.5V, Part2.VCC
